# Fritzing sketch mirror (saved by Fritzing 0.8.7b)
breadboards: 1

parts:
  Anschluß_LED-Strip = Header 4 [package=1x04-1mm-ra]
  Bauteil2 = Arduino Nano (Rev3.0)
  UDS1 = PING Ultrasonic Sensor
  Bauteil3 = Breakout Board for Electret Microphone

nets:
  N1: Anschluß_LED-Strip.2, Bauteil2.D13/SCK
  N2: Anschluß_LED-Strip.3, Bauteil2.D11/MOSI
  GND: Anschluß_LED-Strip.4, Bauteil2.GND, UDS1.GND, Bauteil3.GND
  N3: Bauteil2.D7, UDS1.I/O
  VCC: Bauteil2.5V, UDS1.VCC, Bauteil3.VCC
  N4: Bauteil2.A0, Bauteil3.AUD

custom parts:
  PING Ultrasonic Sensor: The PING)))™ ultrasonic sensor provides an easy method of distance measurement. This sensor is perfect for any number of applications that require you to perform measurements between moving or stationary objects. Interfacing to a microcontroller is a snap. A single I/O pin is used to trigger an ultrasonic burst (well above human hearing) and then "listen" for the echo return pulse. The sensor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
